// Logisim project MaryLadder_8bits_sim.circ as structural Verilog: 1 circuit, main circuit main
module main (
);

  wire and_1_out, and_2_out, and_3_out, and_4_out, and_5_out, and_6_out, and_7_out, and_8_out, and_9_out,
       and_10_out, and_11_out, and_12_out, and_13_out, and_14_out, and_15_out, and_16_out, dipswitch_1_sw1,
       dipswitch_1_sw2, dipswitch_1_sw3, dipswitch_1_sw4, dipswitch_1_sw5, dipswitch_1_sw6, dipswitch_1_sw7,
       dipswitch_1_sw8, dipswitch_2_sw1, dipswitch_2_sw2, dipswitch_2_sw3, dipswitch_2_sw4, dipswitch_2_sw5,
       dipswitch_2_sw6, dipswitch_2_sw7, dipswitch_2_sw8, dipswitch_3_p1, or_1_out, or_2_out, or_3_out,
       or_4_out, or_5_out, or_6_out, or_7_out, or_8_out, xor_1_out, xor_2_out, xor_3_out, xor_4_out,
       xor_5_out, xor_6_out, xor_7_out, xor_8_out, xor_9_out, xor_10_out, xor_11_out, xor_12_out, xor_13_out,
       xor_14_out, xor_15_out, xor_16_out, xor_17_out, xor_18_out, xor_19_out, xor_20_out, xor_21_out,
       xor_22_out, xor_23_out, xor_24_out;

  LED led_1 (.in(dipswitch_1_sw1));
  LED led_2 (.in(dipswitch_1_sw2));
  LED led_3 (.in(dipswitch_2_sw1));
  LED led_4 (.in(dipswitch_2_sw2));
  LED led_5 (.in(or_8_out));
  LED led_6 (.in(xor_24_out));
  LED led_7 (.in(dipswitch_1_sw3));
  LED led_8 (.in(dipswitch_1_sw4));
  DipSwitch dipswitch_1 (
    .sw1(dipswitch_1_sw1), .sw2(dipswitch_1_sw2), .sw3(dipswitch_1_sw3), .sw4(dipswitch_1_sw4),
    .sw5(dipswitch_1_sw5), .sw6(dipswitch_1_sw6), .sw7(dipswitch_1_sw7), .sw8(dipswitch_1_sw8));
  LED led_9 (.in(dipswitch_2_sw3));
  LED led_10 (.in(dipswitch_2_sw4));
  DipSwitch dipswitch_2 (
    .sw1(dipswitch_2_sw1), .sw2(dipswitch_2_sw2), .sw3(dipswitch_2_sw3), .sw4(dipswitch_2_sw4),
    .sw5(dipswitch_2_sw5), .sw6(dipswitch_2_sw6), .sw7(dipswitch_2_sw7), .sw8(dipswitch_2_sw8));
  // DipSwitch #(.number(2)) dipswitch_3: pin names not known; wires that end beside it: dipswitch_3_p1
  LED led_11 (.in(dipswitch_3_p1));
  xor xor_1 (xor_1_out, dipswitch_2_sw1, dipswitch_3_p1);
  xor xor_2 (xor_2_out, dipswitch_2_sw2, dipswitch_3_p1);
  xor xor_3 (xor_3_out, dipswitch_2_sw3, dipswitch_3_p1);
  xor xor_4 (xor_4_out, dipswitch_2_sw4, dipswitch_3_p1);
  LED led_12 (.in(xor_22_out));
  LED led_13 (.in(xor_21_out));
  LED led_14 (.in(xor_23_out));
  LED led_15 (.in(dipswitch_1_sw5));
  LED led_16 (.in(dipswitch_1_sw6));
  LED led_17 (.in(dipswitch_1_sw7));
  LED led_18 (.in(dipswitch_2_sw5));
  LED led_19 (.in(dipswitch_2_sw6));
  LED led_20 (.in(dipswitch_2_sw7));
  LED led_21 (.in(xor_16_out));
  LED led_22 (.in(xor_15_out));
  LED led_23 (.in(dipswitch_1_sw8));
  LED led_24 (.in(dipswitch_2_sw8));
  xor xor_5 (xor_5_out, dipswitch_2_sw5, dipswitch_3_p1);
  xor xor_6 (xor_6_out, dipswitch_2_sw6, dipswitch_3_p1);
  xor xor_7 (xor_7_out, dipswitch_2_sw7, dipswitch_3_p1);
  xor xor_8 (xor_8_out, dipswitch_2_sw8, dipswitch_3_p1);
  LED led_25 (.in(xor_14_out));
  LED led_26 (.in(xor_13_out));
  xor xor_9 (xor_9_out, dipswitch_1_sw8, xor_8_out);
  xor xor_10 (xor_10_out, dipswitch_1_sw7, xor_7_out);
  xor xor_11 (xor_11_out, dipswitch_1_sw6, xor_6_out);
  xor xor_12 (xor_12_out, dipswitch_1_sw5, xor_5_out);
  xor xor_13 (xor_13_out, xor_9_out, dipswitch_3_p1);
  and and_1 (and_1_out, dipswitch_3_p1, xor_9_out);
  or or_1 (or_1_out, and_1_out, and_2_out);
  and and_2 (and_2_out, xor_8_out, dipswitch_1_sw8);
  xor xor_14 (xor_14_out, xor_10_out, or_1_out);
  and and_3 (and_3_out, or_1_out, xor_10_out);
  or or_2 (or_2_out, and_3_out, and_4_out);
  and and_4 (and_4_out, xor_7_out, dipswitch_1_sw7);
  xor xor_15 (xor_15_out, xor_11_out, or_2_out);
  and and_5 (and_5_out, or_2_out, xor_11_out);
  or or_3 (or_3_out, and_5_out, and_6_out);
  and and_6 (and_6_out, xor_6_out, dipswitch_1_sw6);
  xor xor_16 (xor_16_out, xor_12_out, or_3_out);
  and and_7 (and_7_out, or_3_out, xor_12_out);
  or or_4 (or_4_out, and_7_out, and_8_out);
  and and_8 (and_8_out, xor_5_out, dipswitch_1_sw5);
  xor xor_17 (xor_17_out, dipswitch_1_sw4, xor_4_out);
  and and_9 (and_9_out, or_4_out, xor_17_out);
  and and_10 (and_10_out, xor_4_out, dipswitch_1_sw4);
  xor xor_18 (xor_18_out, dipswitch_1_sw3, xor_3_out);
  and and_11 (and_11_out, or_5_out, xor_18_out);
  and and_12 (and_12_out, xor_3_out, dipswitch_1_sw3);
  xor xor_19 (xor_19_out, dipswitch_1_sw2, xor_2_out);
  and and_13 (and_13_out, or_6_out, xor_19_out);
  and and_14 (and_14_out, xor_2_out, dipswitch_1_sw2);
  xor xor_20 (xor_20_out, dipswitch_1_sw1, xor_1_out);
  and and_15 (and_15_out, or_7_out, xor_20_out);
  and and_16 (and_16_out, xor_1_out, dipswitch_1_sw1);
  xor xor_21 (xor_21_out, xor_17_out, or_4_out);
  or or_5 (or_5_out, and_9_out, and_10_out);
  xor xor_22 (xor_22_out, xor_18_out, or_5_out);
  or or_6 (or_6_out, and_11_out, and_12_out);
  xor xor_23 (xor_23_out, xor_19_out, or_6_out);
  or or_7 (or_7_out, and_13_out, and_14_out);
  xor xor_24 (xor_24_out, xor_20_out, or_7_out);
  or or_8 (or_8_out, and_15_out, and_16_out);

  // Notes on the sheet:
  //   A7
  //   A6
  //   128
  //   64
  //   B7
  //   B6
  //   128
  //   64
  //   S8
  //   S7
  //   255
  //   128
  //   A
  //   A5
  //   A4
  //   32
  //   16
  //   8
  //   B
  //   B5
  //   B4
  //   32
  //   16
  //   8
  //   S
  //   S5
  //   S4
  //   S6
  //   32
  //   16
  //   64
  //   [1st Input]
  //   A3
  //   A2
  //   A1
  //   4
  //   2
  //   [2nd Input]
  //   B3
  //   B2
  //   B1
  //   4
  //   2
  //   [Sum Output]
  //   S3
  //   S2
  //   8
  //   4
  //   2
  //   A0
  //   1
  //   B0
  //   1
  //   S1
  //   S0
  //   1
  //   A0
  //   XB0
  //   K
  //   A1
  //   XB1
  //   A2
  //   XB2
  //   A3
  //   XB3
  //   S0
  //   S1
  //   S2
  //   S3
  //   A4
  //   XB4
  //   A5
  //   XB5
  //   A6
  //   XB6
  //   A7
  //   XB7
  //   S4
  //   S5
  //   S6
  //   S7
  //   S8
endmodule
